// Logisim project project.circ as structural Verilog: 3 circuits, main circuit main
module main (
);

  wire ALURE, ARE1, ARE2, ARE3, Awe, BRE1, BRE2, BRE3, Bwe, CLK, CRE1, CRE2, CRE3, Cwe, decoder_1_out4,
       decoder_1_out5, decoder_1_out6, decoder_1_out7, decoder_3_out6, decoder_3_out7, DRE1, DRE2, DRE3, Dwe,
       ImmRE, ImmWE, not_1_out, RST;
  wire [1:0] REASel, REBSel;
  wire [2:0] RESel, WESel;
  wire [7:0] A_q, AIn, AOut2, AOut3, B_q, Bus8Memory, C_q, D_q, Imm_q, ImmIn, pull_resistor_1_node,
       register_1_q, register_2_q;
  wire [7:5] Stage1_data;
  wire [7:6] Stage2_data;
  wire [15:0] Bus16;

  Clock clock_1 (.out(CLK));
  Button Reset (.out(RST));
  Register #(.width(16)) SP (.clk(CLK), .clr(RST));  // open: D, en, Q
  Register #(.width(16)) SI (.clk(CLK), .clr(RST));  // open: D, en, Q
  Register #(.width(16)) DI (.clk(CLK), .clr(RST));  // open: D, en, Q
  Counter #(.max('hffff), .width(16)) PC (
    .clr(RST), .load(1'b0), .up(1'b1), .count(1'b1), .clk(CLK), .Q(Bus16));  // open: D, carry
  Register Imm (.D(ImmIn), .en(ImmWE), .clk(CLK), .Q(Imm_q), .clr(RST));
  ROM #(.addrWidth(16)) MainMemory_temp (.addr(Bus16), .data(Bus8Memory));
  assign AIn = ImmRE ? Imm_q : 8'bz;  // Controlled_Buffer controlled_buffer_1
  DualPortRegister8 TL ();  // open: OutputA, OutputB, InputA, InputB, LoadA, LoadB, CLK, RST, EnableA, EnableB
  Register A (.D(AIn), .en(Awe), .clk(CLK), .Q(A_q), .clr(RST));
  Register C (.D(AIn), .en(Cwe), .clk(CLK), .Q(C_q), .clr(RST));
  assign AIn = ARE1 ? A_q : 8'bz;  // Controlled_Buffer controlled_buffer_2
  assign AOut2 = ARE2 ? A_q : 8'bz;  // Controlled_Buffer controlled_buffer_3
  assign AOut3 = ARE3 ? A_q : 8'bz;  // Controlled_Buffer controlled_buffer_4
  assign AIn = CRE1 ? C_q : 8'bz;  // Controlled_Buffer controlled_buffer_5
  assign AOut2 = CRE2 ? C_q : 8'bz;  // Controlled_Buffer controlled_buffer_6
  assign AOut3 = CRE3 ? C_q : 8'bz;  // Controlled_Buffer controlled_buffer_7
  Register B (.D(AIn), .en(Bwe), .clk(CLK), .Q(B_q), .clr(RST));
  Register D (.D(AIn), .en(Dwe), .clk(CLK), .Q(D_q), .clr(RST));
  assign AIn = BRE1 ? B_q : 8'bz;  // Controlled_Buffer controlled_buffer_8
  assign AOut2 = BRE2 ? B_q : 8'bz;  // Controlled_Buffer controlled_buffer_9
  assign AOut3 = BRE3 ? B_q : 8'bz;  // Controlled_Buffer controlled_buffer_10
  assign AIn = DRE1 ? D_q : 8'bz;  // Controlled_Buffer controlled_buffer_11
  assign AOut2 = DRE2 ? D_q : 8'bz;  // Controlled_Buffer controlled_buffer_12
  assign AOut3 = DRE3 ? D_q : 8'bz;  // Controlled_Buffer controlled_buffer_13
  Pull_Resistor pull_resistor_1 (.node(pull_resistor_1_node));
  // LedBar #(.inputtype("row")) ledbar_1: pin names not known; wires that end beside it: pull_resistor_1_node
  Register register_1 (.D(pull_resistor_1_node), .en(1'b1), .clk(CLK), .Q(register_1_q), .clr(RST));
  assign pull_resistor_1_node = not_1_out ? Bus8Memory : 8'bz;  // Controlled_Buffer controlled_buffer_14
  not not_1 (not_1_out, ImmWE);
  Register register_2 (.D(register_1_q), .en(1'b1), .clk(CLK), .Q(register_2_q), .clr(RST));
  ROM Stage1 (.addr(register_1_q), .data({Stage1_data, ImmWE, REBSel, REASel}));
  ROM Stage2 (.addr(register_2_q), .data({Stage2_data, RESel, WESel}));
  Decoder #(.enable("false"), .select(3)) decoder_1 (
    .out0(Awe), .out1(Bwe), .out2(Cwe), .out3(Dwe), .out4(decoder_1_out4), .out5(decoder_1_out5),
    .out6(decoder_1_out6), .out7(decoder_1_out7), .sel(WESel));
  Decoder #(.enable("false"), .select(2)) decoder_2 (.out0(ARE2), .out1(BRE2), .out2(CRE2), .out3(DRE2), .sel(REASel));
  Decoder #(.enable("false"), .select(3)) decoder_3 (
    .out0(ARE1), .out1(BRE1), .out2(CRE1), .out3(DRE1), .out4(ImmRE), .out5(ALURE), .out6(decoder_3_out6),
    .out7(decoder_3_out7), .sel(RESel));
  Decoder #(.enable("false"), .select(2)) decoder_4 (.out0(ARE3), .out1(BRE3), .out2(CRE3), .out3(DRE3), .sel(REBSel));
  ALU alu_1 (.A(AOut2), .B(AOut3), .ALURE(ALURE), .CLK(CLK));  // open: Y

  // Other names for the same wires on the sheet: BOut2[7:0] = AOut2; Bus8ALUA[7:0] = AOut2; COut2[7:0] = AOut2;
  //   DOut2[7:0] = AOut2; BOut3[7:0] = AOut3; Bus8ALUB[7:0] = AOut3; COut3[7:0] = AOut3; DOut3[7:0] = AOut3;
  //   AOut1[7:0] = AIn; BIn[7:0] = AIn; BOut1[7:0] = AIn; Bus8Main[7:0] = AIn; CIn[7:0] = AIn; COut1[7:0] = AIn;
  //   DIn[7:0] = AIn; DOut1[7:0] = AIn; ImmOut[7:0] = AIn; PCout[15:0] = Bus16; ROMAddrIn[15:0] = Bus16;
  //   ConstIn[7:0] = Bus8Memory; PipelineIn[7:0] = Bus8Memory; ROMDataout[7:0] = Bus8Memory

  // Notes on the sheet:
  //   contents of MainMemory_temp (hex, n*v repeats v):
  //   0 1 1 2 2 3 3 4 4
  //   contents of Stage1 (hex, n*v repeats v):
  //   0 4*1
  //   contents of Stage2 (hex, n*v repeats v):
  //   0 42
endmodule

module ALU (
  input  [7:0] A,
  input  [7:0] B,
  input  ALURE,
  input  CLK,
  output [7:0] Y
);

  wire [7:0] adder_1_out, register_1_q, register_2_q;

  Shifter shifter_1 ();  // open: in, dist, out
  Shifter #(.shift("lr")) shifter_2 ();  // open: in, dist, out
  // NOT_Gate not_1 is placed but not wired
  Register register_1 (.D(A), .Q(register_1_q), .clk(CLK));  // open: en, clr
  Register register_2 (.D(B), .Q(register_2_q), .clk(CLK));  // open: en, clr
  assign Y = ALURE ? adder_1_out : 8'bz;  // Controlled_Buffer controlled_buffer_1
  Adder adder_1 (.a(register_1_q), .b(register_2_q), .out(adder_1_out));  // open: cin, cout
endmodule

module DualPortRegister8 (
  input  EnableA,
  input  [7:0] InputA,
  input  [7:0] InputB,
  input  LoadA,
  input  EnableB,
  input  LoadB,
  input  CLK,
  input  RST,
  output [7:0] OutputA,
  output [7:0] OutputB
);

  wire and_1_out;
  wire [7:0] multiplexer_1_out, register_1_q;

  Multiplexer #(.width(8)) multiplexer_1 (.in0(InputA), .in1(InputB), .out(multiplexer_1_out), .sel(LoadA));
  Register register_1 (.D(multiplexer_1_out), .en(and_1_out), .clk(CLK), .Q(register_1_q), .clr(RST));
  and and_1 (and_1_out, LoadA, LoadB);
  assign OutputA = EnableA ? register_1_q : 8'bz;  // Controlled_Buffer controlled_buffer_1
  assign OutputB = EnableB ? register_1_q : 8'bz;  // Controlled_Buffer controlled_buffer_2
endmodule
